// Logisim project RelogioDigital.circ as structural Verilog: 1 circuit, main circuit main
module main (
);

  wire and_1_out, and_2_out, and_3_out, and_4_out, and_5_out, and_6_out, and_7_out, and_8_out, and_9_out,
       and_10_out, and_11_out, and_12_out, and_13_out, clock_1_out, j_k_ff_12_qn, j_k_ff_19_qn, or_1_out,
       or_2_out, or_3_out, or_4_out;
  wire [0:0] j_k_ff_10_q;
  wire [2:0] j_k_ff_2_q, j_k_ff_14_q;
  wire [3:0] j_k_ff_1_q, j_k_ff_4_q, j_k_ff_13_q;

  J_K_Flip_Flop #(.trigger("falling")) j_k_ff_1 (
    .J(or_2_out), .clk(and_12_out), .K(or_2_out), .Q(j_k_ff_1_q[0]));  // open: Qn, preset, en, reset
  or or_1 (or_1_out, or_3_out, and_4_out);
  J_K_Flip_Flop #(.trigger("falling")) j_k_ff_2 (
    .J(or_2_out), .clk(j_k_ff_1_q[3]), .K(or_2_out), .Q(j_k_ff_2_q[0]), .reset(and_4_out));  // open: Qn, preset, en
  and and_1 (and_1_out, j_k_ff_12_qn, j_k_ff_1_q[0]);
  J_K_Flip_Flop #(.trigger("falling")) j_k_ff_3 (
    .J(and_1_out), .clk(and_12_out), .K(j_k_ff_1_q[0]), .Q(j_k_ff_1_q[1]));  // open: Qn, preset, en, reset
  J_K_Flip_Flop #(.trigger("falling")) j_k_ff_4 (
    .J(or_2_out), .clk(or_1_out), .K(or_2_out), .Q(j_k_ff_4_q[0]), .reset(or_3_out));  // open: Qn, preset, en
  and and_2 (and_2_out, j_k_ff_1_q[1], j_k_ff_1_q[0]);
  and and_3 (and_3_out, j_k_ff_1_q[1], j_k_ff_1_q[0]);
  J_K_Flip_Flop #(.trigger("falling")) j_k_ff_5 (
    .J(or_2_out), .clk(j_k_ff_4_q[0]), .K(or_2_out), .Q(j_k_ff_4_q[1]), .reset(or_3_out));  // open: Qn, preset, en
  J_K_Flip_Flop #(.trigger("falling")) j_k_ff_6 (
    .J(or_2_out), .clk(j_k_ff_2_q[0]), .K(or_2_out), .Q(j_k_ff_2_q[1]), .reset(and_4_out));  // open: Qn, preset, en
  J_K_Flip_Flop #(.trigger("falling")) j_k_ff_7 (
    .J(and_2_out), .clk(and_12_out), .K(and_2_out), .Q(j_k_ff_1_q[2]));  // open: Qn, preset, en, reset
  J_K_Flip_Flop #(.trigger("falling")) j_k_ff_8 (
    .J(or_2_out), .clk(j_k_ff_4_q[1]), .K(or_2_out), .Q(j_k_ff_4_q[2]), .reset(or_3_out));  // open: Qn, preset, en
  J_K_Flip_Flop #(.trigger("falling")) j_k_ff_9 (
    .J(or_2_out), .clk(j_k_ff_2_q[1]), .K(or_2_out), .Q(j_k_ff_2_q[2]), .reset(and_4_out));  // open: Qn, preset, en
  and and_4 (and_4_out, j_k_ff_2_q[1], j_k_ff_2_q[2]);
  or or_2 (or_2_out, j_k_ff_1_q[3], j_k_ff_12_qn);
  and and_5 (and_5_out, j_k_ff_1_q[2], and_3_out);
  Clock clock_1 (.out(clock_1_out));
  J_K_Flip_Flop #(.trigger("falling")) j_k_ff_10 (
    .J(or_2_out), .clk(or_3_out), .K(or_2_out), .Q(j_k_ff_10_q[0]));  // open: Qn, preset, en, reset
  J_K_Flip_Flop #(.trigger("falling")) j_k_ff_11 (
    .J(or_2_out), .clk(j_k_ff_4_q[2]), .K(or_2_out), .Q(j_k_ff_4_q[3]), .reset(or_3_out));  // open: Qn, preset, en
  or or_3 (or_3_out, and_6_out, and_7_out);
  J_K_Flip_Flop #(.trigger("falling")) j_k_ff_12 (
    .J(and_5_out), .clk(and_12_out), .K(j_k_ff_1_q[0]), .Q(j_k_ff_1_q[3]), .Qn(j_k_ff_12_qn));  // open: preset, en, reset
  J_K_Flip_Flop #(.trigger("falling")) j_k_ff_13 (
    .J(or_4_out), .clk(clock_1_out), .K(or_4_out), .Q(j_k_ff_13_q[0]));  // open: Qn, preset, en, reset
  and and_6 (and_6_out, j_k_ff_10_q[0], and_9_out);
  and and_7 (and_7_out, j_k_ff_4_q[1], j_k_ff_4_q[3]);
  and and_8 (and_8_out, j_k_ff_19_qn, j_k_ff_13_q[0]);
  Hex_Digit_Display hex_digit_display_1 (.value(j_k_ff_4_q));  // open: dp
  Hex_Digit_Display hex_digit_display_2 (.value({3'b000, j_k_ff_10_q[0]}));  // open: dp
  and and_9 (and_9_out, j_k_ff_4_q[1], j_k_ff_4_q[0]);
  J_K_Flip_Flop #(.trigger("falling")) j_k_ff_14 (
    .J(or_4_out), .clk(j_k_ff_13_q[3]), .K(or_4_out), .Q(j_k_ff_14_q[0]), .reset(and_12_out));  // open: Qn, preset, en
  J_K_Flip_Flop #(.trigger("falling")) j_k_ff_15 (
    .J(and_8_out), .clk(clock_1_out), .K(j_k_ff_13_q[0]), .Q(j_k_ff_13_q[1]));  // open: Qn, preset, en, reset
  and and_10 (and_10_out, j_k_ff_13_q[1], j_k_ff_13_q[0]);
  Hex_Digit_Display hex_digit_display_3 (.value({1'b0, j_k_ff_2_q}));  // open: dp
  J_K_Flip_Flop #(.trigger("falling")) j_k_ff_16 (
    .J(or_4_out), .clk(j_k_ff_14_q[0]), .K(or_4_out), .Q(j_k_ff_14_q[1]), .reset(and_12_out));  // open: Qn, preset, en
  and and_11 (and_11_out, j_k_ff_13_q[1], j_k_ff_13_q[0]);
  J_K_Flip_Flop #(.trigger("falling")) j_k_ff_17 (
    .J(and_11_out), .clk(clock_1_out), .K(and_11_out), .Q(j_k_ff_13_q[2]));  // open: Qn, preset, en, reset
  Hex_Digit_Display hex_digit_display_4 (.value({1'b0, j_k_ff_14_q}));  // open: dp
  Hex_Digit_Display hex_digit_display_5 (.value(j_k_ff_1_q));  // open: dp
  J_K_Flip_Flop #(.trigger("falling")) j_k_ff_18 (
    .J(or_4_out), .clk(j_k_ff_14_q[1]), .K(or_4_out), .Q(j_k_ff_14_q[2]), .reset(and_12_out));  // open: Qn, preset, en
  and and_12 (and_12_out, j_k_ff_14_q[1], j_k_ff_14_q[2]);
  or or_4 (or_4_out, j_k_ff_13_q[3], j_k_ff_19_qn);
  and and_13 (and_13_out, j_k_ff_13_q[2], and_10_out);
  Hex_Digit_Display hex_digit_display_6 (.value(j_k_ff_13_q));  // open: dp
  J_K_Flip_Flop #(.trigger("falling")) j_k_ff_19 (
    .J(and_13_out), .clk(clock_1_out), .K(j_k_ff_13_q[0]), .Q(j_k_ff_13_q[3]), .Qn(j_k_ff_19_qn));  // open: preset, en, reset

  // Notes on the sheet:
  //   :
  //   :
endmodule
