// Logisim project Semaforo.circ as structural Verilog: 1 circuit, main circuit main
module main (
);

  wire and_1_out, and_2_out, and_3_out, and_4_out, and_5_out, and_6_out, and_7_out, and_8_out, and_9_out,
       clock_1_out, clock_2_out, NoT_2_out, NoT_out;

  Clock #(.lowDuration(2)) clock_1 (.out(clock_1_out));
  Clock #(.highDuration(2)) clock_2 (.out(clock_2_out));
  not NoT (NoT_out, clock_1_out);
  not NoT_2 (NoT_2_out, clock_2_out);
  and and_1 (and_1_out, NoT_out, NoT_2_out);
  and and_2 (and_2_out, NoT_out, clock_2_out);
  and and_3 (and_3_out, clock_2_out, clock_1_out);
  and and_4 (and_4_out, clock_2_out, clock_1_out);
  and and_5 (and_5_out, NoT_out, clock_2_out);
  and and_6 (and_6_out, NoT_out, NoT_2_out);
  LED led_1 (.in(and_1_out));
  LED led_2 (.in(and_2_out));
  LED led_3 (.in(and_3_out));
  LED led_4 (.in(and_4_out));
  LED led_5 (.in(and_5_out));
  LED led_6 (.in(and_6_out));
  and and_7 (and_7_out, NoT_2_out, NoT_out);
  and and_8 (and_8_out, clock_2_out, clock_1_out);
  and and_9 (and_9_out, clock_2_out, NoT_out);
  LED led_7 (.in(and_7_out));
  LED led_8 (.in(and_8_out));
  LED led_9 (.in(and_9_out));
endmodule
