// Logisim project começa do 12.circ as structural Verilog: 1 circuit, main circuit main
module main (
);

  wire _1_out, and_1_out, and_2_out, button_1_out, j_k_ff_1_q, j_k_ff_2_q, j_k_ff_3_q, j_k_ff_4_q, or_1_out;

  Clock _1 (.out(_1_out));
  Button button_1 (.out(button_1_out));
  and and_1 (and_1_out, j_k_ff_1_q, j_k_ff_2_q);
  or or_1 (or_1_out, and_1_out, j_k_ff_4_q);
  J_K_Flip_Flop j_k_ff_1 (
    .J(1'b1), .clk(_1_out), .K(1'b1), .Q(j_k_ff_1_q), .reset(button_1_out));  // open: Qn, preset, en
  J_K_Flip_Flop j_k_ff_2 (
    .J(j_k_ff_1_q), .clk(_1_out), .K(j_k_ff_1_q), .Q(j_k_ff_2_q), .reset(button_1_out));  // open: Qn, preset, en
  J_K_Flip_Flop j_k_ff_3 (
    .J(and_1_out), .clk(_1_out), .K(or_1_out), .Q(j_k_ff_3_q), .preset(button_1_out));  // open: Qn, en, reset
  J_K_Flip_Flop j_k_ff_4 (
    .J(and_2_out), .clk(_1_out), .K(j_k_ff_3_q), .Q(j_k_ff_4_q), .preset(button_1_out));  // open: Qn, en, reset
  and and_2 (and_2_out, j_k_ff_1_q, j_k_ff_2_q, j_k_ff_3_q);
  LED _1_2 (.in(j_k_ff_1_q));
  LED _2 (.in(j_k_ff_2_q));
  LED _4 (.in(j_k_ff_3_q));
  LED _8 (.in(j_k_ff_4_q));
endmodule
